# Fritzing sketch PMS breadboard (saved by Fritzing 1.0.6)
breadboards: 1

parts:
  Part1 = Adafruit HUZZAH32 ESP32 Feather [part_number="Adafruit #3405"]
  MOD1 = MT3608 Boost No usb
  Part2 = Adafruit DPS310 Precision Barometric Pressure and Altitude Sensor [part_number="Adafruit #4494"]
  Part3 = Adafruit SCD4x [part_number="Adafruit #5187"]
  U1 = Sensirion SPS30 particle sensor [chip_label=SPS30 package="SIP (Single Inline) [THT]"]  # not connected
  U2 = LIPO-2000mAh [package=lipo-2000]  # not connected

nets:
  GND: Part1.GND, MOD1.IN_(-), MOD1.OUT_(-), Part2.GND, Part3.GND
  N1: Part1.VBAT, MOD1.IN_(+)
  N2: Part1.SCL, Part2.SCK/SCL, Part3.SCL
  N3: Part1.SDA, Part2.SDI/SDA, Part3.SDA
  VCC: Part2.VCC, Part3.VCC

custom parts:
  MT3608 Boost No usb: Chip- MT3608 / B6289 DC to DC step up, power booster module. With adjustable output voltage. Current- 2A . || Input voltage- 2V-24V || Output voltage- 5V-28V Input interface- Inversed polarity- NO. || Led indicator- No.
  Adafruit DPS310 Precision Barometric Pressure and Altitude Sensor: How high are you right now? If you had a precision altitude sensor, you would know for sure! The DPS310 sensor from Infineon a high precision barometric sensor, perfect for measuring altitude changes with a up to ±0.002 hPa (or ±0.02 m) precision high precision mode and ± 1 hPa absolute accuracy. That means you can know your absolute altitude with 1 meter accuracy when you set the sea-level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
  Adafruit SCD4x: Take a deep breath in...now slowly breathe out. Mmm isn't it wonderful? All that air around us, which we bring into our lungs, extracts oxygen from and then breathes out carbon dioxide. CO2 is essential for life on this planet we call Earth - we and plants take turns using and emitting CO2 in an elegant symbiosis. But it's important to keep that CO2 balanced - you don't want too much around,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
