# Fritzing sketch SPS30breadboard (saved by Fritzing 1.0.6)
breadboards: 1

parts:
  HUZZAH32_ESP32 = Adafruit HUZZAH32 ESP32 Feather [part_number="Adafruit #3405"]
  MT3608_Boost_Converter = MT3608 Boost No usb
  DPS310 = Adafruit DPS310 Precision Barometric Pressure and Altitude Sensor [part_number="Adafruit #4494"]
  SCD40 = Adafruit SCD4x [part_number="Adafruit #5187"]
  2000mAh_Lipo_Battery = LIPO-2000mAh [package=lipo-2000]  # not connected
  SPS30 = Sensirion SPS30 particle sensor [chip_label=SPS30 package="SIP (Single Inline) [THT]"]
  R2 = Resistor [tolerance=±1% power=0.25W resistance=10k package=THT]
  R1 = Resistor [tolerance=±1% resistance=10k package="0402 [SMD]"]
  PTS645_Button = Pushbutton [package="[SMD]"]
  3-foot_Bi-colour_LED = DUO LED RW [current=0.030A color="Red (633nm)" package="8 mm [THT]"]
  R3 = Resistor [tolerance=±5% resistance=330 package="2010 [SMD]"]
  R4 = Resistor [tolerance=±5% resistance=330 package="2010 [SMD]"]

nets:
  GND: HUZZAH32_ESP32.GND, MT3608_Boost_Converter.IN_(-), MT3608_Boost_Converter.OUT_(-), DPS310.GND, SCD40.GND, SPS30.SEL, SPS30.GND, PTS645_Button.Pin_3, PTS645_Button.Pin_4, 3-foot_Bi-colour_LED.common_cathode
  VCC: HUZZAH32_ESP32.3.3V, DPS310.VCC, SCD40.VCC, R2.Pin_1, R1.Pin_1
  N1: HUZZAH32_ESP32.VBAT, MT3608_Boost_Converter.IN_(+)
  N2: HUZZAH32_ESP32.IO27_A10, PTS645_Button.Pin_2
  N3: HUZZAH32_ESP32.IO33_A9, R4.Pin_1
  N4: HUZZAH32_ESP32.IO32_A7, R3.Pin_1
  N5: HUZZAH32_ESP32.SCL, DPS310.SCK/SCL, SCD40.SCL, SPS30.TX, R2.Pin_0
  N6: HUZZAH32_ESP32.SDA, DPS310.SDI/SDA, SCD40.SDA, SPS30.RX, R1.Pin_0
  N7: MT3608_Boost_Converter.OUT_(+), SPS30.VCC
  N8: 3-foot_Bi-colour_LED.red_anode, R3.Pin_0
  N9: 3-foot_Bi-colour_LED.white_anode, R4.Pin_0

custom parts:
  MT3608 Boost No usb: Chip- MT3608 / B6289 DC to DC step up, power booster module. With adjustable output voltage. Current- 2A . || Input voltage- 2V-24V || Output voltage- 5V-28V Input interface- Inversed polarity- NO. || Led indicator- No.
  Adafruit DPS310 Precision Barometric Pressure and Altitude Sensor: How high are you right now? If you had a precision altitude sensor, you would know for sure! The DPS310 sensor from Infineon a high precision barometric sensor, perfect for measuring altitude changes with a up to ±0.002 hPa (or ±0.02 m) precision high precision mode and ± 1 hPa absolute accuracy. That means you can know your absolute altitude with 1 meter accuracy when you set the sea-level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
  Adafruit SCD4x: Take a deep breath in...now slowly breathe out. Mmm isn't it wonderful? All that air around us, which we bring into our lungs, extracts oxygen from and then breathes out carbon dioxide. CO2 is essential for life on this planet we call Earth - we and plants take turns using and emitting CO2 in an elegant symbiosis. But it's important to keep that CO2 balanced - you don't want too much around,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
